# Fritzing sketch UselessBox (saved by Fritzing 0.9.3b)
breadboards: 1

parts:
  Bauteil1 = Arduino Nano (Rev3.0)
  Q1 = TRANSISTOR_NPN [package=to-92-ammo]
  D1 = Diode [package=sod523]
  R1 = Resistor [tolerance=±5% resistance=220 package=THT]
  J1 = female pin header, 3 pins [form="♀ (female)"]
  J2 = female pin header, 3 pins [form="♀ (female)"]
  J3 = female pin header, 2 pins [form="♀ (female)"]
  J4 = female pin header, 2 pins [form="♀ (female)"]
  C1 = Electrolytic Capacitor [capacitance=1µF package="100 mil [THT, electrolytic]"]
  J5 = female pin header, 5 pins [form="♀ (female)"]
  J6 = female pin header, 2 pins [form="♀ (female)"]
  R4 = Resistor [tolerance=±5% resistance=220 package=THT]
  R5 = Resistor [tolerance=±5% resistance=220 package=THT]

nets:
  N1: Bauteil1.GND, Q1.E, J1.pin3, J2.pin3, J3.pin2, J4.pin1, C1.-, J5.pin5, R4.Pin_0
  N2: Bauteil1.D4, R1.Pin_0
  N3: Bauteil1.D5, J5.pin3
  N4: Bauteil1.D6, J5.pin2
  N5: Bauteil1.D7, J5.pin1
  N6: Bauteil1.D8, J3.pin1
  N7: Bauteil1.D9, J2.pin1
  N8: Bauteil1.D10, J1.pin1
  N9: Bauteil1.VIN, J6.pin2, R5.Pin_0
  N10: Bauteil1.5V, J1.pin2, J2.pin2, C1.+
  N11: Bauteil1.A0, R4.Pin_1, R5.Pin_1
  N12: Q1.B, R1.Pin_1
  N13: Q1.C, D1.A
  N14: J4.pin2, J6.pin1
